// Logisim project 2bitmultiplier.circ as structural Verilog: 1 circuit, main circuit main
module main (
  input  [1:0] in_1,
  input  [1:0] in_2
);

  wire and_1_out, and_2_out, and_3_out, and_4_out, and_5_out, and_6_out, xor_1_out, xor_2_out;

  and and_1 (and_1_out, in_2[1], in_1[1]);
  and and_2 (and_2_out, in_2[0], in_1[0]);
  and and_3 (and_3_out, in_2[1], in_1[0]);
  and and_4 (and_4_out, in_2[0], in_1[1]);
  xor xor_1 (xor_1_out, and_3_out, and_4_out);
  and and_5 (and_5_out, and_4_out, and_3_out);
  xor xor_2 (xor_2_out, and_1_out, and_5_out);
  and and_6 (and_6_out, and_1_out, and_5_out);
  LED led_1 (.in(and_2_out));
  LED led_2 (.in(xor_1_out));
  LED led_3 (.in(xor_2_out));
  LED led_4 (.in(and_6_out));

  // Notes on the sheet:
  //   A0
  //   A1
  //   B0
  //   B1
endmodule
