// Logisim project 4bitadder.circ as structural Verilog: 1 circuit, main circuit main
module main (
  input  in_1,
  input  [3:0] in_2,
  input  [3:0] B
);

  wire and_1_out, and_2_out, and_3_out, and_4_out, and_5_out, and_6_out, and_7_out, and_8_out, or_1_out,
       or_2_out, or_3_out, or_4_out, xor_1_out, xor_2_out, xor_3_out, xor_4_out, xor_5_out, xor_6_out,
       xor_7_out, xor_8_out, xor_9_out, xor_10_out, xor_11_out, xor_12_out;

  xor xor_1 (xor_1_out, B[0], in_1);
  xor xor_2 (xor_2_out, B[1], in_1);
  xor xor_3 (xor_3_out, B[2], in_1);
  xor xor_4 (xor_4_out, B[3], in_1);
  xor xor_5 (xor_5_out, in_2[0], xor_1_out);
  and and_1 (and_1_out, in_2[0], xor_1_out);
  xor xor_6 (xor_6_out, in_2[1], xor_2_out);
  and and_2 (and_2_out, in_2[1], xor_2_out);
  xor xor_7 (xor_7_out, in_2[2], xor_3_out);
  and and_3 (and_3_out, in_2[2], xor_3_out);
  xor xor_8 (xor_8_out, in_2[3], xor_4_out);
  and and_4 (and_4_out, in_2[3], xor_4_out);
  and and_5 (and_5_out, or_4_out, xor_6_out);
  xor xor_9 (xor_9_out, xor_5_out, in_1);
  and and_6 (and_6_out, in_1, xor_5_out);
  xor xor_10 (xor_10_out, xor_6_out, or_4_out);
  xor xor_11 (xor_11_out, xor_7_out, or_1_out);
  and and_7 (and_7_out, or_1_out, xor_7_out);
  xor xor_12 (xor_12_out, xor_8_out, or_2_out);
  and and_8 (and_8_out, or_2_out, xor_8_out);
  or or_1 (or_1_out, and_5_out, and_2_out);
  or or_2 (or_2_out, and_7_out, and_3_out);
  or or_3 (or_3_out, and_8_out, and_4_out);
  or or_4 (or_4_out, and_6_out, and_1_out);
  LED led_1 (.in(xor_9_out));
  LED led_2 (.in(xor_10_out));
  LED led_3 (.in(xor_11_out));
  LED led_4 (.in(xor_12_out));
  LED led_5 (.in(or_3_out));

  // Notes on the sheet:
  //   A
  //   A0
  //   B0
  //   A1
  //   B1
  //   A2
  //   B2
  //   A3
  //   B3
  //   K
  //   S0
  //   S1
  //   S2
  //   S3
  //   C
endmodule
