// Logisim project 8bitaddersubtractor.circ as structural Verilog: 3 circuits, main circuit main
module main (
  input  in_1,
  input  in_2,
  input  [8:0] in_3,
  input  [8:0] in_4,
  input  in_5
);

  wire and_1_out, and_2_out, and_3_out, and_4_out, and_5_out, and_6_out, and_7_out, and_8_out, and_9_out,
       and_10_out, and_11_out, and_12_out, and_13_out, and_14_out, and_15_out, and_16_out, and_17_out,
       and_18_out, or_1_out, or_2_out, or_3_out, or_4_out, or_5_out, or_6_out, or_7_out, or_8_out,
       twocomplement_1_b0, twocomplement_1_b1, twocomplement_1_b2, twocomplement_1_b3, twocomplement_1_b4,
       twocomplement_1_b5, twocomplement_1_b6, twocomplement_1_b7, twocomplement_2_b0, twocomplement_2_b1,
       twocomplement_2_b2, twocomplement_2_b3, twocomplement_2_b4, twocomplement_2_b5, twocomplement_2_b6,
       twocomplement_2_b7, xor_1_out, xor_2_out, xor_3_out, xor_4_out, xor_5_out, xor_6_out, xor_7_out,
       xor_8_out, xor_9_out, xor_10_out, xor_11_out, xor_12_out, xor_13_out, xor_14_out, xor_15_out,
       xor_16_out, xor_17_out, xor_18_out, xor_19_out, xor_20_out, xor_21_out, xor_22_out, xor_23_out,
       xor_24_out;

  and and_1 (and_1_out, in_3[8], in_2);
  and and_2 (and_2_out, in_4[8], in_5);
  twocomplement twocomplement_1 (
    .in_1(and_1_out), .a0(in_3[0]), .a1(in_3[1]), .a2(in_3[2]), .a3(in_3[3]), .a4(in_3[4]), .a5(in_3[5]),
    .a6(in_3[6]), .a7(in_3[7]), .a8(in_3[8]), .b0(twocomplement_1_b0), .b1(twocomplement_1_b1),
    .b2(twocomplement_1_b2), .b3(twocomplement_1_b3), .b4(twocomplement_1_b4), .b5(twocomplement_1_b5),
    .b6(twocomplement_1_b6), .b7(twocomplement_1_b7));
  twocomplement twocomplement_2 (
    .in_1(and_2_out), .a0(in_4[0]), .a1(in_4[1]), .a2(in_4[2]), .a3(in_4[3]), .a4(in_4[4]), .a5(in_4[5]),
    .a6(in_4[6]), .a7(in_4[7]), .a8(in_4[8]), .b0(twocomplement_2_b0), .b1(twocomplement_2_b1),
    .b2(twocomplement_2_b2), .b3(twocomplement_2_b3), .b4(twocomplement_2_b4), .b5(twocomplement_2_b5),
    .b6(twocomplement_2_b6), .b7(twocomplement_2_b7));
  xor xor_1 (xor_1_out, twocomplement_2_b0, in_1);
  xor xor_2 (xor_2_out, twocomplement_2_b1, in_1);
  xor xor_3 (xor_3_out, twocomplement_2_b2, in_1);
  xor xor_4 (xor_4_out, twocomplement_2_b3, in_1);
  xor xor_5 (xor_5_out, twocomplement_2_b4, in_1);
  xor xor_6 (xor_6_out, twocomplement_2_b5, in_1);
  xor xor_7 (xor_7_out, twocomplement_2_b6, in_1);
  xor xor_8 (xor_8_out, twocomplement_2_b7, in_1);
  xor xor_9 (xor_9_out, twocomplement_1_b0, xor_1_out);
  and and_3 (and_3_out, twocomplement_1_b0, xor_1_out);
  xor xor_10 (xor_10_out, twocomplement_1_b1, xor_2_out);
  and and_4 (and_4_out, twocomplement_1_b1, xor_2_out);
  xor xor_11 (xor_11_out, twocomplement_1_b2, xor_3_out);
  and and_5 (and_5_out, twocomplement_1_b2, xor_3_out);
  xor xor_12 (xor_12_out, twocomplement_1_b3, xor_4_out);
  and and_6 (and_6_out, twocomplement_1_b3, xor_4_out);
  xor xor_13 (xor_13_out, twocomplement_1_b4, xor_5_out);
  and and_7 (and_7_out, twocomplement_1_b4, xor_5_out);
  xor xor_14 (xor_14_out, twocomplement_1_b5, xor_6_out);
  and and_8 (and_8_out, twocomplement_1_b5, xor_6_out);
  xor xor_15 (xor_15_out, twocomplement_1_b6, xor_7_out);
  and and_9 (and_9_out, twocomplement_1_b6, xor_7_out);
  xor xor_16 (xor_16_out, twocomplement_1_b7, xor_8_out);
  and and_10 (and_10_out, twocomplement_1_b7, xor_8_out);
  xor xor_17 (xor_17_out, xor_9_out, in_1);
  and and_11 (and_11_out, xor_9_out, in_1);
  xor xor_18 (xor_18_out, xor_10_out, or_1_out);
  and and_12 (and_12_out, xor_10_out, or_1_out);
  xor xor_19 (xor_19_out, xor_11_out, or_2_out);
  and and_13 (and_13_out, xor_11_out, or_2_out);
  xor xor_20 (xor_20_out, xor_12_out, or_3_out);
  and and_14 (and_14_out, xor_12_out, or_3_out);
  xor xor_21 (xor_21_out, xor_13_out, or_4_out);
  and and_15 (and_15_out, xor_13_out, or_4_out);
  xor xor_22 (xor_22_out, xor_14_out, or_5_out);
  and and_16 (and_16_out, xor_14_out, or_5_out);
  xor xor_23 (xor_23_out, xor_15_out, or_6_out);
  and and_17 (and_17_out, xor_15_out, or_6_out);
  xor xor_24 (xor_24_out, xor_16_out, or_7_out);
  and and_18 (and_18_out, xor_16_out, or_7_out);
  or or_1 (or_1_out, and_11_out, and_3_out);
  or or_2 (or_2_out, and_12_out, and_4_out);
  or or_3 (or_3_out, and_13_out, and_5_out);
  or or_4 (or_4_out, and_14_out, and_6_out);
  or or_5 (or_5_out, and_15_out, and_7_out);
  or or_6 (or_6_out, and_16_out, and_8_out);
  or or_7 (or_7_out, and_17_out, and_9_out);
  or or_8 (or_8_out, and_18_out, and_10_out);
  LED led_1 (.in(xor_17_out));
  LED led_2 (.in(xor_18_out));
  LED led_3 (.in(xor_19_out));
  LED led_4 (.in(xor_20_out));
  LED led_5 (.in(xor_21_out));
  LED led_6 (.in(xor_22_out));
  LED led_7 (.in(xor_23_out));
  LED led_8 (.in(xor_24_out));
  LED led_9 (.in(or_8_out));

  // Notes on the sheet:
  //   Subtract
endmodule

module twocomplement (
  input  in_1,
  input  a0,
  input  a1,
  input  a2,
  input  a3,
  input  a4,
  input  a5,
  input  a6,
  input  a7,
  input  a8,
  output b0,
  output b1,
  output b2,
  output b3,
  output b4,
  output b5,
  output b6,
  output b7
);

  wire fulladder_1_out_5, fulladder_2_out_5, fulladder_3_out_5, fulladder_4_out_5, fulladder_5_out_5,
       fulladder_6_out_5, fulladder_7_out_5, xor_1_out, xor_2_out, xor_3_out, xor_4_out, xor_5_out,
       xor_6_out, xor_7_out, xor_8_out;

  xor xor_1 (xor_1_out, a0, a8);
  xor xor_2 (xor_2_out, a1, a8);
  xor xor_3 (xor_3_out, a2, a8);
  xor xor_4 (xor_4_out, a3, a8);
  xor xor_5 (xor_5_out, a4, a8);
  xor xor_6 (xor_6_out, a5, a8);
  xor xor_7 (xor_7_out, a6, a8);
  xor xor_8 (xor_8_out, a7, a8);
  fulladder fulladder_1 (.in_1(xor_1_out), .in_2(in_1), .out_4(b0), .out_5(fulladder_1_out_5));  // open: in_3
  fulladder fulladder_2 (
    .in_1(xor_2_out), .in_2(fulladder_1_out_5), .out_4(b1), .out_5(fulladder_2_out_5));  // open: in_3
  fulladder fulladder_3 (
    .in_1(xor_3_out), .in_2(fulladder_2_out_5), .out_4(b2), .out_5(fulladder_3_out_5));  // open: in_3
  fulladder fulladder_4 (
    .in_1(xor_4_out), .in_2(fulladder_3_out_5), .out_4(b3), .out_5(fulladder_4_out_5));  // open: in_3
  fulladder fulladder_5 (
    .in_1(xor_5_out), .in_2(fulladder_4_out_5), .out_4(b4), .out_5(fulladder_5_out_5));  // open: in_3
  fulladder fulladder_6 (
    .in_1(xor_6_out), .in_2(fulladder_5_out_5), .out_4(b5), .out_5(fulladder_6_out_5));  // open: in_3
  fulladder fulladder_7 (
    .in_1(xor_7_out), .in_2(fulladder_6_out_5), .out_4(b6), .out_5(fulladder_7_out_5));  // open: in_3
  fulladder fulladder_8 (.in_1(xor_8_out), .in_2(fulladder_7_out_5), .out_4(b7));  // open: in_3, out_5
endmodule

module fulladder (
  input  in_1,
  input  in_2,
  input  in_3,
  output out_4,
  output out_5
);

  wire and_1_out, and_2_out, xor_1_out;

  xor xor_1 (xor_1_out, in_1, in_2);
  and and_1 (and_1_out, in_1, in_2);
  xor xor_2 (out_4, xor_1_out, in_3);
  and and_2 (and_2_out, xor_1_out, in_3);
  or or_1 (out_5, and_2_out, and_1_out);
endmodule
