// Logisim project counters.circ as structural Verilog: 1 circuit, main circuit main
module main (
  input  in_1
);

  wire binary_to_bcd_converter_1_p2, binary_to_bcd_converter_1_p4, binary_to_bcd_converter_1_p5, CLOCK,
       comparator_1_eq, comparator_2_eq, comparator_3_eq, j_k_ff_1_q;
  wire [7:0] counter_1_q;

  Clock clock_1 (.out(CLOCK));
  Counter #(.max('hf)) counter_1 (.clr(in_1), .clk(CLOCK), .Q(counter_1_q));  // open: load, up, count, D, carry
  _7_Segment_Display u_7_segment_display_1 ();  // open: g, f, a, b, e, d, c, dp
  // BCD_to_7_Segment_decoder bcd_to_7_segment_decoder_1: pin names not known
  // Binary_to_BCD_converter #(.binvalue(8)) binary_to_bcd_converter_1: pin names not known; wires that end beside it: counter_1_q, binary_to_bcd_converter_1_p2, binary_to_bcd_converter_1_p2, binary_to_bcd_converter_1_p4, binary_to_bcd_converter_1_p5
  _7_Segment_Display u_7_segment_display_2 ();  // open: g, f, a, b, e, d, c, dp
  // BCD_to_7_Segment_decoder bcd_to_7_segment_decoder_2: pin names not known; wires that end beside it: binary_to_bcd_converter_1_p4
  Comparator comparator_1 (.a({8{1'b0}}), .b(counter_1_q), .eq(comparator_1_eq));  // open: gt, lt
  Comparator comparator_2 (.a(8'h2), .b(counter_1_q), .eq(comparator_2_eq));  // open: gt, lt
  Comparator comparator_3 (.a(8'ha), .b(counter_1_q), .eq(comparator_3_eq));  // open: gt, lt
  _7_Segment_Display u_7_segment_display_3 ();  // open: g, f, a, b, e, d, c, dp
  // BCD_to_7_Segment_decoder bcd_to_7_segment_decoder_3: pin names not known; wires that end beside it: binary_to_bcd_converter_1_p5
  LED led_1 (.in(comparator_1_eq));
  J_K_Flip_Flop j_k_ff_1 (
    .J(comparator_2_eq), .K(comparator_3_eq), .clk(CLOCK), .Q(j_k_ff_1_q));  // open: Qn, preset, reset
  // Buzzer buzzer_1: pin names not known; wires that end beside it: 14'h533, comparator_1_eq
  // Digital_Oscilloscope #(.nState(20)) digital_oscilloscope_1: pin names not known; wires that end beside it: CLOCK, comparator_1_eq, j_k_ff_1_q
endmodule
