// Logisim project diceRoll.circ as structural Verilog: 1 circuit, main circuit main
module main (
  output [3:0] out_1
);

  wire and_1_out, and_2_out, button_1_out, clock_1_out, clock_2_out, d_ff_1_q, or_1_out;

  D_Flip_Flop d_ff_1 (.D(or_1_out), .clk(clock_1_out), .Q(d_ff_1_q), .reset(d_ff_1_q));  // open: Qn, preset
  Clock clock_1 (.out(clock_1_out));
  Clock clock_2 (.out(clock_2_out));
  Button button_1 (.out(button_1_out));
  or or_1 (or_1_out, out_1[3], and_1_out);
  Random #(.width(4)) random_1 (.clr(d_ff_1_q), .next(clock_2_out), .clk(button_1_out), .out(out_1));
  and and_1 (and_1_out, out_1[2], and_2_out);
  and and_2 (and_2_out, out_1[1], out_1[0]);
  _7_Segment_Display u_7_segment_display_1 ();  // open: g, f, a, b, e, d, c, dp
  // BCD_to_7_Segment_decoder bcd_to_7_segment_decoder_1: pin names not known; wires that end beside it: out_1
endmodule
